# Fritzing sketch InfinityGoggles (saved by Fritzing 0.9.2b)

parts:
  FLORA1 = Adafruit_Flora
  LPD8806_RGB_LED_Strip1 = LPD8806 RGB LED Strip
  Part1 = FLORA LSM9DS0
  LPD8806_RGB_LED_Strip2 = LPD8806 RGB LED Strip
  BATT1 = 3xAAA Switchable Battery Pack w/Bare Wire  # not connected

nets:
  N1: FLORA1.connector1, Part1.GND
  N2: FLORA1.connector2, Part1.SCL
  N3: FLORA1.connector3, Part1.SDA
  N4: FLORA1.connector4, Part1.3.3V
  N5: FLORA1.connector5, LPD8806_RGB_LED_Strip2.DI
  N6: FLORA1.connector6, LPD8806_RGB_LED_Strip2.CI
  N7: FLORA1.connector7, LPD8806_RGB_LED_Strip2.GND
  +5V: FLORA1.connector8, LPD8806_RGB_LED_Strip1.+5V, LPD8806_RGB_LED_Strip2.+5V
  N8: FLORA1.connector10, LPD8806_RGB_LED_Strip1.DI
  N9: FLORA1.connector11, LPD8806_RGB_LED_Strip1.GND
  N10: FLORA1.connector12, LPD8806_RGB_LED_Strip1.CI

custom parts:
  LPD8806 RGB LED Strip: Digitally addressable RGB LED strip
  FLORA LSM9DS0: Add motion, direction and orientation sensing to your wearable FLORA project with this high precision 9-DOF sensors. Inside are three sensors, one is a classic 3-axis accelerometer, which can tell you which direction is down towards the Earth (by measuring gravity) or how fast the board is accelerating in 3D space. The other is a 3-axis magnetometer that can sense where the strongest magnetic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
  3xAAA Switchable Battery Pack w/Bare Wire: 3xAAA Switchable Battery Pack w/Bare Wire Connectors
